# Fritzing sketch usb-jtag-adapter (saved by Fritzing 1.0.1rc)
circuit board: 6.22223cm x 2.86679cm
perfboards: 1

parts:
  Bauteil1 = Adafruit FT232H Breakout - USB C and STEMMA QT [part_number="Adafruit #2264"]
  J1 = shrouded pin header, 10 pins [form="♂ (shrouded male)"]

nets:
  N1: Bauteil1.GND, J1.pin6, J1.pin10
  N2: Bauteil1.D0/SCL/SCK, J1.pin1
  N3: Bauteil1.D1/SDA/MOSI, J1.pin5
  N4: Bauteil1.D2/SDA/MISO, J1.pin2
  N5: Bauteil1.D3, J1.pin3

custom parts:
  Adafruit FT232H Breakout - USB C and STEMMA QT: Wouldn't it be cool to drive a tiny OLED display, read a color sensor, or even just flash some LEDs directly from your computer? Sure you can program an Arduino or Trinket to talk to these devices and your computer, but why can't your computer just talk to those devices and sensors itself? Well, now your computer can talk to devices using the Adafruit FT232H breakout board! What can the FT232H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
